# Fritzing sketch usbmux (saved by Fritzing 0.9.5d)

parts:
  KY-1 = Keyes Relay [package=THT]
  X1 = USB Connectors [package=usb-minib]
  JP2 = USB_MICROB_PLUG [package=micro-b-th]
  WeMos_D1_Mini1 = WeMos D1 Mini
  U1 = TS3USB221 [package=so016]
  JP3 = Header 4 [package=screwterminal-3.5mm-4_lock]
  X3 = USB Connectors [package=usb-minib]

nets:
  N1: KY-1.signal, WeMos_D1_Mini1.D7
  N2: KY-1.power, WeMos_D1_Mini1.5V
  N3: KY-1.ground, WeMos_D1_Mini1.G
  N4: KY-1.C, JP3.1, JP3.2
  N5: KY-1.NO, JP3.3, JP3.4
  N6: X1.D+, U1.1D+
  N7: X1.D-, U1.1D-
  N8: X1.GND, U1.GND#8
  N9: X1.VBUS, U1.VCC#11
  N10: JP2.VCC, U1.VCC#0
  N11: JP2.D-, U1.D-
  N12: JP2.D+, U1.D+
  N13: JP2.ID, WeMos_D1_Mini1.D0
  N14: JP2.GND, U1.GND#3
  N15: WeMos_D1_Mini1.D5, U1.OE
  N16: WeMos_D1_Mini1.D6, U1.S
  N17: U1.GND#12, X3.GND
  N18: U1.2D+, X3.D+
  N19: U1.2D-, X3.D-
  N20: U1.VCC#15, X3.VBUS

notes:
  POWER INPUT
  POWER OUTPUT
  PWR_SUPPLY/CMD_SERIAL
  USB INPUT-CH1
  USB INPUT-CH0
  USB OUTPUT

custom parts:
  Keyes Relay: The Keyes 5V relay module is suitable for SCM development, home appliance control. It uses a 5V~12V TIL control signal which can control DC / AC signal.
  TS3USB221: TS3USB221 High-speed USB 2.0 (480-Mbps) 1:2 multiplexer – demultiplexer switch with single enable
